# Fritzing sketch Diagram Wiring and Schematic Wiring (saved by Fritzing 0.9.3b)
breadboards: 1

parts:
  PWR_SUPPLY_24V = Power plug
  U1 = ESP8266 NodeMCU LoLin base
  A1 = DM860A Stepper Motor Driver
  M_X = Stepper Motor - Bipolar
  PWR_SUPPLY_24V_2 = Power plug
  A2 = DM860A Stepper Motor Driver
  M_Z = Stepper Motor - Bipolar
  PWR_SUPPLY_24V_3 = Power plug
  A3 = DM860A Stepper Motor Driver
  M_Y = Stepper Motor - Bipolar

nets:
  N1: PWR_SUPPLY_24V.VCC, A1.VDC
  GND: PWR_SUPPLY_24V.GND, A1.GND
  N2: U1.GND1-0, U1.GND3-0, A1.DIR-(DIR), A1.PUL-(PUL), A2.DIR-(DIR), A2.PUL-(PUL), A3.DIR-(DIR), A3.PUL-(PUL)
  N3: U1.D0-2, U1.D0-3, A1.PUL+(+5V)
  N4: U1.D1-2, A1.DIR+(+5V)
  N5: U1.D2-0, U1.D2-1, A3.DIR+(+5V)
  N6: U1.D3-0, U1.D3-1, A3.PUL+(+5V)
  N7: U1.D4-0, U1.D4-2, A2.DIR+(+5V)
  N8: U1.D5-0, U1.D5-1, U1.D5-2, A2.PUL+(+5V)
  N9: A1.B-, M_X.D
  N10: A1.B+, M_X.B
  N11: A1.A-, M_X.C
  N12: A1.A+, M_X.A
  GND_2: PWR_SUPPLY_24V_2.GND, A2.GND
  N13: PWR_SUPPLY_24V_2.VCC, A2.VDC
  N14: A2.B-, M_Z.D
  N15: A2.B+, M_Z.B
  N16: A2.A-, M_Z.C
  N17: A2.A+, M_Z.A
  GND_3: PWR_SUPPLY_24V_3.GND, A3.GND
  N18: PWR_SUPPLY_24V_3.VCC, A3.VDC
  N19: A3.B-, M_Y.D
  N20: A3.B+, M_Y.B
  N21: A3.A-, M_Y.C
  N22: A3.A+, M_Y.A

custom parts:
  ESP8266 NodeMCU LoLin base: ESP8266 based NodeMCU Base
  DM860A Stepper Motor Driver: DM860A is a type of two-phase hybrid stepping motor driver, The drive voltage of which is from 24VDC to 80VDC. It is designed for use with 2-phase hybrid stepper motor of all kinds with 57mm to 110mm outside diameter and less than 8.0A phase current. Mar 2023: Correct pcb layerId as the part won't save correctly in a .fzz file as is.
